# Fritzing sketch MQ2_ADC_and_Raspberry_pi (saved by Fritzing 0.9.3b)

parts:
  Raspberry_Pi_3 = Raspberry Pi 3 [part_number=RPI-3-V1.2]
  Part1 = MQ-3 breakout
  Part2 = Adafruit ADS1015 12Bit I2C ADC [part_number="Adafruit #1083"]
  R3 = Resistor [tolerance=±5% resistance=1k package=THT]
  R4 = Resistor [tolerance=±5% resistance=1k package=THT]
  R5 = Resistor [tolerance=±5% resistance=1k package=THT]

nets:
  N1: Raspberry_Pi_3.GPIO2, Part2.SDA
  N2: Raspberry_Pi_3.GPIO3, Part2.SCL
  3V3: Raspberry_Pi_3.3V3, Part2.VDD
  GND: Raspberry_Pi_3.GND, Part1.GND, Part2.ADDR, Part2.GND, R4.Pin_0, R5.Pin_1
  5V: Raspberry_Pi_3.5V, Part1.VCC
  N3: Part1.AO, R3.Pin_1
  N4: Part2.AIN0, R5.Pin_0

custom parts:
  MQ-3 breakout: Alcohol sensor is capable of detecting alcohol (ethanol) particles on itself and gives the information in digital form back to us to manipulate with it. SKU:101251 • Voltage: 5V DC • Power: max 750mW • Measurement range: 0.04-4mg/L
  Adafruit ADS1015 12Bit I2C ADC: For microcontrollers without an analog-to-digital converter or when you want a higher-precision ADC, the ADS1015 provides 12-bit precision at 3300 samples/second over I2C. The chip can be configured as 4 single-ended input channels, or two differential channels. As a nice bonus, it even includes a programmable gain amplifier, up to x16, to help boost up smaller single/differential signals to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
