# Fritzing sketch RFID_RC522_and_Raspberry_pi (saved by Fritzing 0.9.3b)

parts:
  Part1 = RFID-RC522 [part_number=101218]
  Raspberry_Pi_2 = Raspberry Pi 3 [part_number=RPI-3-V1.2]

nets:
  N1: Part1.SDA, Raspberry_Pi_2.GPIO8
  N2: Part1.SCK, Raspberry_Pi_2.GPIO11
  N3: Part1.MOSI, Raspberry_Pi_2.GPIO10
  N4: Part1.MISO, Raspberry_Pi_2.GPIO9
  N5: Part1.IRQ, Raspberry_Pi_2.GPIO24
  GND: Part1.GND, Raspberry_Pi_2.GND
  N6: Part1.RST, Raspberry_Pi_2.GPIO25
  3.3V: Part1.3.3V, Raspberry_Pi_2.3V3
